# Fritzing sketch fritzing (saved by Fritzing 0.9.4)

parts:
  WeMos_D1_Mini = WeMos D1 Mini
  Taster_2_(Auswahl) = Round Pushbutton
  LCD_HD44780 = LCD screen
  LCD_I2C_Adapter = LCM1602 IIC [package="DIP (Dual Inline) [THT]"]
  MHZ19 = MH-Z19 CO2 sensor [part_number=MH-Z19]
  JP3 = Header 4 [package=screwterminal-3.5mm-4_lock]
  Taster_1_(Menü) = Round Pushbutton

nets:
  5V: WeMos_D1_Mini.5V, LCD_I2C_Adapter.VCC
  N1: WeMos_D1_Mini.D1, LCD_I2C_Adapter.SCL
  N2: WeMos_D1_Mini.D2, LCD_I2C_Adapter.SDA
  N3: WeMos_D1_Mini.D3, Taster_1_(Menü).leg0
  N4: WeMos_D1_Mini.D5, MHZ19.TX, JP3.3
  N5: WeMos_D1_Mini.D6, MHZ19.RX, JP3.4
  N6: WeMos_D1_Mini.D8, Taster_2_(Auswahl).leg1
  GND: WeMos_D1_Mini.G, LCD_I2C_Adapter.GND, MHZ19.GND, JP3.2, Taster_1_(Menü).leg1
  N7: Taster_2_(Auswahl).leg0, MHZ19.Vin, JP3.1
  VSS: LCD_HD44780.VSS, LCD_I2C_Adapter.VSS
  VDD: LCD_HD44780.VDD, LCD_I2C_Adapter.VDD
  N8: LCD_HD44780.V0, LCD_I2C_Adapter.V0
  N9: LCD_HD44780.RS, LCD_I2C_Adapter.RS
  N10: LCD_HD44780.R/W, LCD_I2C_Adapter.RW
  N11: LCD_HD44780.E, LCD_I2C_Adapter.E
  N12: LCD_HD44780.DB0, LCD_I2C_Adapter.D0
  N13: LCD_HD44780.DB1, LCD_I2C_Adapter.D1
  N14: LCD_HD44780.DB2, LCD_I2C_Adapter.D2
  N15: LCD_HD44780.DB3, LCD_I2C_Adapter.D3
  N16: LCD_HD44780.DB4, LCD_I2C_Adapter.D4
  N17: LCD_HD44780.DB5, LCD_I2C_Adapter.D5
  N18: LCD_HD44780.DB6, LCD_I2C_Adapter.D6
  N19: LCD_HD44780.DB7, LCD_I2C_Adapter.D7
  N20: LCD_HD44780.LED+, LCD_I2C_Adapter.A
  N21: LCD_HD44780.LED-, LCD_I2C_Adapter.K
  N22: LCD_I2C_Adapter.LED_A, LCD_I2C_Adapter.LED_B

notes:
  MHZ19
  - RX (blau)
  - TX (grün)
  - GND (schwarz)
  - Vin (rot)

custom parts:
  LCM1602 IIC: I2C-Module to use a 1602 or 2004 LCD on with the wire.h libory Serial LCD Modul
